// Logisim project control-logic.circ as structural Verilog: 1 circuit, main circuit control_logic
module control_logic (
  input  [31:0] Instruction,
  input  BrEq,
  input  BrLt,
  output PCSel,
  output RegWEn,
  output [2:0] ImmSel,
  output BrUn,
  output ASel,
  output BSel,
  output [3:0] ALUSel,
  output MemWEn,
  output [1:0] WBSel
);

  wire and_1_out, and_2_out, and_3_out, and_4_out, and_5_out, and_6_out, and_7_out, and_8_out, and_9_out,
       and_10_out, and_11_out, and_12_out, and_13_out, and_14_out, and_15_out, and_16_out, comparator_1_eq,
       comparator_2_eq, comparator_3_eq, comparator_4_eq, comparator_5_eq, comparator_6_eq, comparator_7_eq,
       comparator_8_eq, comparator_9_eq, comparator_10_eq, comparator_11_eq, comparator_12_eq,
       comparator_13_eq, comparator_14_eq, comparator_15_eq, comparator_16_eq, comparator_17_eq,
       comparator_18_eq, comparator_19_eq, comparator_20_eq, comparator_21_eq, comparator_22_eq,
       comparator_23_eq, comparator_24_eq, comparator_25_eq, comparator_26_eq, comparator_27_eq,
       comparator_28_eq, comparator_29_eq, comparator_30_eq, comparator_31_eq, comparator_32_eq,
       comparator_33_eq, comparator_34_eq, comparator_35_eq, comparator_36_eq, comparator_37_eq,
       comparator_38_eq, comparator_39_eq, comparator_40_eq, comparator_41_eq, comparator_42_eq,
       comparator_43_eq, comparator_44_eq, comparator_45_eq, comparator_46_eq, comparator_47_eq,
       comparator_48_eq, comparator_49_eq, comparator_50_eq, comparator_51_eq, comparator_52_eq,
       comparator_53_eq, comparator_54_eq, comparator_55_eq, comparator_56_eq, comparator_57_eq,
       comparator_58_eq, comparator_59_eq, comparator_60_eq, multiplexer_7_out, not_1_out, not_2_out,
       not_3_out, not_4_out, or_1_out, or_2_out;
  wire [1:0] I_Select_Load;
  wire [2:0] B_Select, priority_encoder_3_out, S_Select;
  wire [3:0] I_Select, Ins_Type, R_Select;
  wire [5:0] multiplexer_1_out, multiplexer_2_out, multiplexer_3_out, multiplexer_4_out, multiplexer_5_out,
       multiplexer_6_out;
  wire [15:14] rom_1_data;

  Comparator #(.width(7)) comparator_1 (.a(Instruction[6:0]), .b(7'b0010011), .eq(comparator_1_eq));  // open: gt, lt
  Comparator #(.width(7)) comparator_2 (.a(Instruction[6:0]), .b(7'b0110011), .eq(comparator_2_eq));  // open: gt, lt
  Comparator #(.width(7)) comparator_3 (.a(Instruction[6:0]), .b(7'b1100011), .eq(comparator_3_eq));  // open: gt, lt
  Comparator #(.width(7)) comparator_4 (.a(Instruction[6:0]), .b(7'b0000011), .eq(comparator_4_eq));  // open: gt, lt
  Comparator #(.width(7)) comparator_5 (.a(Instruction[6:0]), .b(7'b0100011), .eq(comparator_5_eq));  // open: gt, lt
  Comparator #(.width(7)) comparator_6 (.a(Instruction[6:0]), .b(7'b1101111), .eq(comparator_6_eq));  // open: gt, lt
  Comparator #(.width(7)) comparator_7 (.a(Instruction[6:0]), .b(7'b1100111), .eq(comparator_7_eq));  // open: gt, lt
  Comparator #(.width(7)) comparator_8 (.a(Instruction[6:0]), .b(7'b0010111), .eq(comparator_8_eq));  // open: gt, lt
  Comparator #(.width(7)) comparator_9 (.a(Instruction[6:0]), .b(7'b0110111), .eq(comparator_9_eq));  // open: gt, lt
  Comparator #(.width(3)) comparator_10 (.a(Instruction[14:12]), .b(3'b000), .eq(comparator_10_eq));  // open: gt, lt
  Comparator #(.width(3)) comparator_11 (.a(Instruction[14:12]), .b(3'b010), .eq(comparator_11_eq));  // open: gt, lt
  Comparator #(.width(3)) comparator_12 (.a(Instruction[14:12]), .b(3'b100), .eq(comparator_12_eq));  // open: gt, lt
  Comparator #(.width(3)) comparator_13 (.a(Instruction[14:12]), .b(3'b110), .eq(comparator_13_eq));  // open: gt, lt
  Comparator #(.width(3)) comparator_14 (.a(Instruction[14:12]), .b(3'b111), .eq(comparator_14_eq));  // open: gt, lt
  Comparator #(.width(3)) comparator_15 (.a(Instruction[14:12]), .b(3'b001), .eq(comparator_15_eq));  // open: gt, lt
  Comparator #(.width(3)) comparator_16 (.a(Instruction[14:12]), .b(3'b101), .eq(comparator_16_eq));  // open: gt, lt
  Comparator #(.width(3)) comparator_17 (.a(Instruction[14:12]), .b(3'b101), .eq(comparator_17_eq));  // open: gt, lt
  Comparator #(.width(3)) comparator_18 (.a(Instruction[14:12]), .b(3'b000), .eq(comparator_18_eq));  // open: gt, lt
  Comparator #(.width(3)) comparator_19 (.a(Instruction[14:12]), .b(3'b101), .eq(comparator_19_eq));  // open: gt, lt
  Comparator #(.width(3)) comparator_20 (.a(Instruction[14:12]), .b(3'b111), .eq(comparator_20_eq));  // open: gt, lt
  Comparator #(.width(3)) comparator_21 (.a(Instruction[14:12]), .b(3'b100), .eq(comparator_21_eq));  // open: gt, lt
  Comparator #(.width(3)) comparator_22 (.a(Instruction[14:12]), .b(3'b110), .eq(comparator_22_eq));  // open: gt, lt
  Comparator #(.width(3)) comparator_23 (.a(Instruction[14:12]), .b(3'b001), .eq(comparator_23_eq));  // open: gt, lt
  Comparator #(.width(3)) comparator_24 (.a(Instruction[14:12]), .b(3'b000), .eq(comparator_24_eq));  // open: gt, lt
  Comparator #(.width(3)) comparator_25 (.a(Instruction[14:12]), .b(3'b001), .eq(comparator_25_eq));  // open: gt, lt
  Comparator #(.width(3)) comparator_26 (.a(Instruction[14:12]), .b(3'b010), .eq(comparator_26_eq));  // open: gt, lt
  Comparator #(.width(3)) comparator_27 (.a(Instruction[14:12]), .b(3'b000), .eq(comparator_27_eq));  // open: gt, lt
  Comparator #(.width(3)) comparator_28 (.a(Instruction[14:12]), .b(3'b001), .eq(comparator_28_eq));  // open: gt, lt
  Comparator #(.width(3)) comparator_29 (.a(Instruction[14:12]), .b(3'b010), .eq(comparator_29_eq));  // open: gt, lt
  and and_1 (and_1_out, comparator_15_eq, comparator_30_eq);
  Comparator #(.width(7)) comparator_30 (.a(Instruction[31:25]), .b({7{1'b0}}), .eq(comparator_30_eq));  // open: gt, lt
  and and_2 (and_2_out, comparator_16_eq, comparator_31_eq);
  Comparator #(.width(7)) comparator_31 (.a(Instruction[31:25]), .b({7{1'b0}}), .eq(comparator_31_eq));  // open: gt, lt
  and and_3 (and_3_out, comparator_17_eq, comparator_32_eq);
  Comparator #(.width(7)) comparator_32 (
    .a(Instruction[31:25]), .b(7'b0100000), .eq(comparator_32_eq));  // open: gt, lt
  Priority_Encoder #(.select(4)) priority_encoder_1 (
    .in0(comparator_1_eq), .in1(comparator_2_eq), .in2(comparator_3_eq), .in3(comparator_4_eq),
    .in4(comparator_5_eq), .in5(comparator_6_eq), .in6(comparator_7_eq), .in7(comparator_8_eq),
    .in8(comparator_9_eq), .out(Ins_Type));  // open: in9, in10, in11, in12, in13, in14, in15, gs, en_out, en_in
  Priority_Encoder priority_encoder_2 (
    .in0(comparator_18_eq), .in1(comparator_19_eq), .in2(comparator_20_eq), .in3(comparator_21_eq),
    .in4(comparator_22_eq), .in5(comparator_23_eq), .out(B_Select));  // open: in6, in7, en_in, gs, en_out
  Priority_Encoder priority_encoder_3 (
    .in0(comparator_24_eq), .in1(comparator_25_eq), .in2(comparator_26_eq), .out(priority_encoder_3_out));  // open: in3, in4, in5, in6, in7, en_in, gs, en_out
  Priority_Encoder priority_encoder_4 (
    .in0(comparator_27_eq), .in1(comparator_28_eq), .in2(comparator_29_eq), .out(S_Select));  // open: in3, in4, in5, in6, in7, en_in, gs, en_out
  Priority_Encoder #(.select(4)) priority_encoder_5 (
    .in0(comparator_10_eq), .in1(comparator_11_eq), .in2(comparator_12_eq), .in3(comparator_13_eq),
    .in4(comparator_14_eq), .in5(and_1_out), .in6(and_2_out), .in7(and_3_out), .out(I_Select));  // open: in8, in9, in10, in11, in12, in13, in14, in15, gs, en_out, en_in
  Bit_Extender #(.in_width(3), .out_width(2)) bit_extender_1 (.in(priority_encoder_3_out), .out(I_Select_Load));
  Multiplexer #(.enable("false"), .select(4), .width(6)) multiplexer_1 (
    .in0(6'b001111), .in1(6'b010001), .in2(6'b010010), .in3(6'b010101), .in4(6'b010110), .in5(6'b010000),
    .in6(6'b010011), .in7(6'b010100), .out(multiplexer_1_out), .sel(I_Select));  // open: in8, in9, in10, in11, in12, in13, in14, in15
  ROM #(.addrWidth(6), .dataWidth(16)) rom_1 (
    .addr(multiplexer_2_out), .data({rom_1_data, WBSel, MemWEn, ALUSel, BSel, ASel, BrUn, ImmSel, RegWEn}));
  Multiplexer #(.enable("false"), .select(4), .width(6)) multiplexer_2 (
    .in0(multiplexer_1_out), .in1(multiplexer_3_out), .in2(multiplexer_4_out), .in3(multiplexer_5_out),
    .in4(multiplexer_6_out), .in5(6'b100010), .in6(6'b100011), .in7(6'b100000), .in8(6'b100001),
    .out(multiplexer_2_out), .sel(Ins_Type));  // open: in9, in10, in11, in12, in13, in14, in15
  Multiplexer #(.enable("false"), .select(4), .width(6)) multiplexer_3 (
    .in0({6{1'b0}}), .in1(6'b000010), .in2(6'b001011), .in3(6'b001010), .in4(6'b000111), .in5(6'b000011),
    .in6(6'b001001), .in7(6'b001000), .in8(6'b000110), .in9(6'b000001), .in10(6'b000100), .in11(6'b000101),
    .out(multiplexer_3_out), .sel(R_Select));  // open: in12, in13, in14, in15
  Comparator #(.width(3)) comparator_33 (.a(Instruction[14:12]), .b(3'b000), .eq(comparator_33_eq));  // open: gt, lt
  Comparator #(.width(3)) comparator_34 (.a(Instruction[14:12]), .b(3'b000), .eq(comparator_34_eq));  // open: gt, lt
  Comparator #(.width(3)) comparator_35 (.a(Instruction[14:12]), .b(3'b111), .eq(comparator_35_eq));  // open: gt, lt
  Comparator #(.width(3)) comparator_36 (.a(Instruction[14:12]), .b(3'b110), .eq(comparator_36_eq));  // open: gt, lt
  Comparator #(.width(3)) comparator_37 (.a(Instruction[14:12]), .b(3'b100), .eq(comparator_37_eq));  // open: gt, lt
  Comparator #(.width(3)) comparator_38 (.a(Instruction[14:12]), .b(3'b001), .eq(comparator_38_eq));  // open: gt, lt
  Comparator #(.width(3)) comparator_39 (.a(Instruction[14:12]), .b(3'b101), .eq(comparator_39_eq));  // open: gt, lt
  Comparator #(.width(3)) comparator_40 (.a(Instruction[14:12]), .b(3'b101), .eq(comparator_40_eq));  // open: gt, lt
  Comparator #(.width(3)) comparator_41 (.a(Instruction[14:12]), .b(3'b010), .eq(comparator_41_eq));  // open: gt, lt
  Comparator #(.width(3)) comparator_42 (.a(Instruction[14:12]), .b(3'b000), .eq(comparator_42_eq));  // open: gt, lt
  Comparator #(.width(3)) comparator_43 (.a(Instruction[14:12]), .b(3'b001), .eq(comparator_43_eq));  // open: gt, lt
  Comparator #(.width(3)) comparator_44 (.a(Instruction[14:12]), .b(3'b011), .eq(comparator_44_eq));  // open: gt, lt
  Multiplexer #(.enable("false"), .select(3), .width(6)) multiplexer_4 (
    .in0(6'b011010), .in1(6'b011101), .in2(6'b011111), .in3(6'b011011), .in4(6'b011110), .in5(6'b011011),
    .out(multiplexer_4_out), .sel(B_Select));  // open: in6, in7
  Comparator #(.width(7)) comparator_45 (.a(Instruction[31:25]), .b({7{1'b0}}), .eq(comparator_45_eq));  // open: gt, lt
  Comparator #(.width(7)) comparator_46 (
    .a(Instruction[31:25]), .b(7'b0100000), .eq(comparator_46_eq));  // open: gt, lt
  Comparator #(.width(7)) comparator_47 (.a(Instruction[31:25]), .b({7{1'b0}}), .eq(comparator_47_eq));  // open: gt, lt
  Comparator #(.width(7)) comparator_48 (.a(Instruction[31:25]), .b({7{1'b0}}), .eq(comparator_48_eq));  // open: gt, lt
  Comparator #(.width(7)) comparator_49 (.a(Instruction[31:25]), .b({7{1'b0}}), .eq(comparator_49_eq));  // open: gt, lt
  Comparator #(.width(7)) comparator_50 (.a(Instruction[31:25]), .b({7{1'b0}}), .eq(comparator_50_eq));  // open: gt, lt
  Comparator #(.width(7)) comparator_51 (
    .a(Instruction[31:25]), .b(7'b0100000), .eq(comparator_51_eq));  // open: gt, lt
  Comparator #(.width(7)) comparator_52 (.a(Instruction[31:25]), .b({7{1'b0}}), .eq(comparator_52_eq));  // open: gt, lt
  Comparator #(.width(7)) comparator_53 (.a(Instruction[31:25]), .b({7{1'b0}}), .eq(comparator_53_eq));  // open: gt, lt
  Comparator #(.width(7)) comparator_54 (
    .a(Instruction[31:25]), .b(7'b0000001), .eq(comparator_54_eq));  // open: gt, lt
  Comparator #(.width(7)) comparator_55 (
    .a(Instruction[31:25]), .b(7'b0000001), .eq(comparator_55_eq));  // open: gt, lt
  Comparator #(.width(7)) comparator_56 (
    .a(Instruction[31:25]), .b(7'b0000001), .eq(comparator_56_eq));  // open: gt, lt
  Multiplexer #(.enable("false"), .select(2), .width(6)) multiplexer_5 (
    .in0(6'b001100), .in1(6'b001101), .in2(6'b001110), .out(multiplexer_5_out), .sel(I_Select_Load));  // open: in3
  Multiplexer #(.enable("false"), .select(3), .width(6)) multiplexer_6 (
    .in0(6'b010111), .in1(6'b011000), .in2(6'b011001), .out(multiplexer_6_out), .sel(S_Select));  // open: in3, in4, in5, in6, in7
  and and_4 (and_4_out, comparator_33_eq, comparator_45_eq);
  and and_5 (and_5_out, comparator_34_eq, comparator_46_eq);
  and and_6 (and_6_out, comparator_35_eq, comparator_47_eq);
  and and_7 (and_7_out, comparator_36_eq, comparator_48_eq);
  and and_8 (and_8_out, comparator_37_eq, comparator_49_eq);
  and and_9 (and_9_out, comparator_38_eq, comparator_50_eq);
  and and_10 (and_10_out, comparator_39_eq, comparator_51_eq);
  and and_11 (and_11_out, comparator_40_eq, comparator_52_eq);
  and and_12 (and_12_out, comparator_41_eq, comparator_53_eq);
  and and_13 (and_13_out, comparator_42_eq, comparator_54_eq);
  and and_14 (and_14_out, comparator_43_eq, comparator_55_eq);
  and and_15 (and_15_out, comparator_44_eq, comparator_56_eq);
  Priority_Encoder #(.select(4)) priority_encoder_6 (
    .in0(and_4_out), .in1(and_5_out), .in2(and_6_out), .in3(and_7_out), .in4(and_8_out), .in5(and_9_out),
    .in6(and_10_out), .in7(and_11_out), .in8(and_12_out), .in9(and_13_out), .in10(and_14_out),
    .in11(and_15_out), .out(R_Select));  // open: in12, in13, in14, in15, gs, en_out, en_in
  Comparator #(.mode("unsigned"), .width(4)) comparator_57 (
    .a(Ins_Type), .b(4'b0010), .eq(comparator_57_eq));  // open: gt, lt
  Multiplexer #(.enable("false"), .select(3)) multiplexer_7 (
    .in0(BrEq), .in1(not_1_out), .in2(not_2_out), .in3(BrLt), .in4(BrLt), .in5(not_3_out),
    .out(multiplexer_7_out), .sel(B_Select));  // open: in6, in7
  not not_1 (not_1_out, BrLt);
  not not_2 (not_2_out, BrLt);
  not not_3 (not_3_out, BrEq);
  and and_16 (and_16_out, comparator_57_eq, multiplexer_7_out);
  Comparator #(.width(32)) comparator_58 (.a(Instruction), .b({32{1'b0}}), .eq(comparator_58_eq));  // open: gt, lt
  or or_1 (or_1_out, and_16_out, or_2_out);
  not not_4 (not_4_out, comparator_58_eq);
  Comparator #(.width(4)) comparator_59 (.a(Ins_Type), .b(4'b0110), .eq(comparator_59_eq));  // open: gt, lt
  Comparator #(.width(4)) comparator_60 (.a(Ins_Type), .b(4'b0101), .eq(comparator_60_eq));  // open: gt, lt
  and and_17 (PCSel, not_4_out, or_1_out);
  or or_2 (or_2_out, comparator_59_eq, comparator_60_eq);

  // Other names for the same wires on the sheet: opcode[6:0] = Instruction[6:0]; func3[2:0] = Instruction[14:12];
  //   func7[6:0] = Instruction[31:25]

  // Notes on the sheet:
  //   INPUTS to your circuit
  //   DON'T CHANGE THE LOCATIONS OF THE INPUTS AND OUTPUTS!
  //   OUTPUT from your circuit
  //   contents of rom_1 (hex, n*v repeats v):
  //   1001 1401 1601 1081 1481 1581 1101 1201 1281 1681 1301 1381 41 41 41 1041 10c1 1141 1241 12c1 16c1
  //   1341 13c1 842 842 842 4*1064 1074 1074 1067 17c7 2069 2041
  //   ROM FOR CONTROL LOGIC
  //   This is only if you choose to do the ROM option
  //   Reminder: If using ROM, use combinational logic for PCSel
endmodule
