// Logisim project cpu.circ as structural Verilog: 1 circuit, main circuit cpu
module cpu (
  input  clk,
  input  [31:0] Instruction,
  input  [31:0] MemReadData,
  output [31:0] MemAddress,
  output [31:0] ProgramCounter,
  output [31:0] ra,
  output [31:0] sp,
  output [31:0] t0,
  output [31:0] t1,
  output [31:0] t2,
  output [31:0] s0,
  output [31:0] s1,
  output [31:0] a0,
  output [3:0] MemWriteMask,
  output [31:0] MemWriteData
);

  wire branch_comp_1_breq, branch_comp_1_brlt, control_logic_1_asel, control_logic_1_brun,
       control_logic_1_bsel, control_logic_1_memwen, control_logic_1_pcsel, control_logic_1_regwen, not_1_out;
  wire [1:0] control_logic_1_wbsel;
  wire [2:0] control_logic_1_immsel;
  wire [3:0] control_logic_1_alusel;
  wire [31:0] adder_1_out, adder_2_out, FinishedData, imm_gen_1_immediate, Ins2, multiplexer_1_out,
       multiplexer_2_out, multiplexer_3_out, multiplexer_4_out, multiplexer_5_out, PC2_q, RegData,
       regfile_1_regreaddata1;

  Adder #(.width(32)) adder_1 (.a(ProgramCounter), .b(32'h4), .out(adder_1_out));  // open: cin, cout
  Register #(.width(32)) PC (.D(multiplexer_1_out), .clk(clk), .Q(ProgramCounter));  // open: en, clr
  Multiplexer #(.enable("false"), .width(32)) multiplexer_1 (
    .in0(adder_1_out), .in1(MemAddress), .out(multiplexer_1_out), .sel(control_logic_1_pcsel));
  not not_1 (not_1_out, control_logic_1_pcsel);
  Register #(.width(32)) PC2 (.D(ProgramCounter), .en(not_1_out), .clk(clk), .Q(PC2_q));  // open: clr
  Register #(.width(32)) Ins (.D(multiplexer_2_out), .clk(clk), .Q(Ins2));  // open: en, clr
  Multiplexer #(.enable("false"), .width(32)) multiplexer_2 (
    .in0(Instruction), .in1(32'h13), .out(multiplexer_2_out), .sel(control_logic_1_pcsel));
  Adder #(.width(32)) adder_2 (.a(PC2_q), .b(32'h4), .out(adder_2_out));  // open: cin, cout
  control_logic control_logic_1 (
    .PCSel(control_logic_1_pcsel), .RegWEn(control_logic_1_regwen), .ImmSel(control_logic_1_immsel),
    .BrUn(control_logic_1_brun), .ASel(control_logic_1_asel), .BSel(control_logic_1_bsel),
    .ALUSel(control_logic_1_alusel), .MemWEn(control_logic_1_memwen), .WBSel(control_logic_1_wbsel),
    .Instruction(Ins2), .BrEq(branch_comp_1_breq), .BrLt(branch_comp_1_brlt));
  regfile regfile_1 (
    .ReadReg1(Ins2[19:15]), .ReadReg2(Ins2[24:20]), .WriteReg(Ins2[11:7]), .RegWriteData(multiplexer_5_out),
    .RegWEn(control_logic_1_regwen), .clk(clk), .ra(ra), .sp(sp), .t0(t0), .t1(t1), .t2(t2), .s0(s0),
    .s1(s1), .a0(a0), .RegReadData1(regfile_1_regreaddata1), .RegReadData2(RegData));
  imm_gen imm_gen_1 (.Instruction(Ins2), .ImmSel(control_logic_1_immsel), .Immediate(imm_gen_1_immediate));
  branch_comp branch_comp_1 (
    .BrData1(regfile_1_regreaddata1), .BrData2(RegData), .BrUn(control_logic_1_brun),
    .BrEq(branch_comp_1_breq), .BrLt(branch_comp_1_brlt));
  Multiplexer #(.enable("false"), .width(32)) multiplexer_3 (
    .in0(regfile_1_regreaddata1), .in1(PC2_q), .out(multiplexer_3_out), .sel(control_logic_1_asel));
  Multiplexer #(.enable("false"), .width(32)) multiplexer_4 (
    .in0(RegData), .in1(imm_gen_1_immediate), .out(multiplexer_4_out), .sel(control_logic_1_bsel));
  alu alu_1 (.ALUResult(MemAddress), .A(multiplexer_3_out), .B(multiplexer_4_out), .ALUSel(control_logic_1_alusel));
  Multiplexer #(.enable("false"), .select(2), .width(32)) multiplexer_5 (
    .in0(FinishedData), .in1(MemAddress), .in2(adder_2_out), .out(multiplexer_5_out),
    .sel(control_logic_1_wbsel));  // open: in3
  partial_store partial_store_1 (
    .Instruction(Ins2), .MemAddress(MemAddress), .DataFromReg(RegData), .MemWEn(control_logic_1_memwen),
    .MemWriteMask(MemWriteMask), .DataToMem(MemWriteData));
  partial_load partial_load_1 (
    .Instruction(Ins2), .MemAddress(MemAddress), .DataFromMem(MemReadData), .DataToReg(FinishedData));

  // Other names for the same wires on the sheet: rd[4:0] = Ins2[11:7]; rs1[4:0] = Ins2[19:15]; rs2[4:0] = Ins2[24:20]

  // Notes on the sheet:
  //   To IMEM
  //   IMEM (do **NOT** move this)
  //   From IMEM
  //   Inputs/Outputs for testing. Do **NOT** move these.
  //   It is OK to move the PC, RegFile, ALU, MEM, Branch Comp, Imm Gen, Partial Load, Partial Store and Control Logic to wherever is most convenient for you when constructing your CPU, and to delete this text
  //   To DMEM
  //   DMEM (do **NOT** move this)
  //   From DMEM
endmodule
