// Logisim project partial-store.circ as structural Verilog: 1 circuit, main circuit partial_store
module partial_store (
  input  [31:0] Instruction,
  input  [31:0] MemAddress,
  input  [31:0] DataFromReg,
  input  MemWEn,
  output [3:0] MemWriteMask,
  output [31:0] DataToMem
);

  wire and_1_out, and_2_out, and_3_out, and_4_out, and_5_out, and_6_out, comparator_1_eq, comparator_2_eq,
       comparator_3_eq, comparator_4_eq, comparator_5_eq, comparator_6_eq, comparator_7_eq;
  wire [2:0] and_7_out, bit_extender_4_out, row;
  wire [31:0] bit_extender_1_out, bit_extender_2_out, bit_extender_3_out;

  Comparator #(.width(3)) comparator_1 (.a(Instruction[14:12]), .b(3'b000), .eq(comparator_1_eq));  // open: gt, lt
  Comparator #(.width(3)) comparator_2 (.a(Instruction[14:12]), .b(3'b001), .eq(comparator_2_eq));  // open: gt, lt
  Comparator #(.width(3)) comparator_3 (.a(Instruction[14:12]), .b(3'b010), .eq(comparator_3_eq));  // open: gt, lt
  Comparator #(.width(2)) comparator_4 (.a(MemAddress[1:0]), .b(2'b00), .eq(comparator_4_eq));  // open: gt, lt
  Comparator #(.width(2)) comparator_5 (.a(MemAddress[1:0]), .b(2'b01), .eq(comparator_5_eq));  // open: gt, lt
  Comparator #(.width(2)) comparator_6 (.a(MemAddress[1:0]), .b(2'b10), .eq(comparator_6_eq));  // open: gt, lt
  Comparator #(.width(2)) comparator_7 (.a(MemAddress[1:0]), .b(2'b11), .eq(comparator_7_eq));  // open: gt, lt
  assign bit_extender_1_out = {{24{DataFromReg[7]}}, DataFromReg[7:0]};  // Bit_Extender bit_extender_1
  and and_1 (and_1_out, comparator_2_eq, comparator_6_eq);
  assign bit_extender_2_out = {{16{DataFromReg[7]}}, {DataFromReg[7:0], {8{1'b0}}}};  // Bit_Extender bit_extender_2
  assign bit_extender_3_out = {{8{DataFromReg[7]}}, {DataFromReg[7:0], {16{1'b0}}}};  // Bit_Extender bit_extender_3
  and and_2 (and_2_out, comparator_2_eq, comparator_4_eq);
  and and_3 (and_3_out, comparator_1_eq, comparator_4_eq);
  and and_4 (and_4_out, comparator_1_eq, comparator_5_eq);
  and and_5 (and_5_out, comparator_1_eq, comparator_6_eq);
  and and_6 (and_6_out, comparator_1_eq, comparator_7_eq);
  Multiplexer #(.enable("false"), .select(3), .width(4)) multiplexer_1 (
    .in0(4'b0000), .in1(4'b0001), .in2(4'b0010), .in3(4'b0100), .in4(4'b1000), .in5(4'b0011), .in6(4'b1100),
    .in7(4'b1111), .out(MemWriteMask), .sel(and_7_out));
  Priority_Encoder priority_encoder_1 (
    .in1(and_3_out), .in2(and_4_out), .in3(and_5_out), .in4(and_6_out), .in5(and_2_out), .in6(and_1_out),
    .in7(comparator_3_eq), .out(row));  // open: in0, en_in, gs, en_out
  Multiplexer #(.enable("false"), .select(3), .width(32)) multiplexer_2 (
    .in0({32{1'b1}}), .in1(bit_extender_1_out), .in2(bit_extender_2_out), .in3(bit_extender_3_out),
    .in4({DataFromReg[7:0], {24{1'b0}}}), .in5({{16{1'b0}}, DataFromReg[15:0]}),
    .in6({DataFromReg[15:0], {16{1'b0}}}), .in7(DataFromReg), .out(DataToMem), .sel(row));
  assign and_7_out = row & bit_extender_4_out;  // AND_Gate and_7, 3 bits wide
  assign bit_extender_4_out = {{2{MemWEn}}, MemWEn};  // Bit_Extender bit_extender_4

  // Other names for the same wires on the sheet: fun3[2:0] = Instruction[14:12]; bot2[1:0] = MemAddress[1:0]

  // Notes on the sheet:
  //   INPUTS to your circuit
  //   DON'T CHANGE THE LOCATIONS OF THE INPUTS AND OUTPUTS!
  //   OUTPUT from your circuit
endmodule
